# Fritzing sketch pcb-source-fritzing (saved by Fritzing 0.9.3b)
circuit board: 2.3cm x 5.3cm
breadboards: 1

parts:
  Součástka1 = Arduino Nano (Rev3.0)
  VCC1 = Battery
  Q1 = Basic FET P-Channel [part_number=IRF1404 package="TO220 [THT]"]
  R1 = Resistor [tolerance=±5% resistance=10k package=THT]
  R2 = Resistor [tolerance=±5% resistance=10k package=THT]
  R3 = Resistor [tolerance=±5% resistance=10k package=THT]
  R4 = Resistor [tolerance=±5% resistance=10k package=THT]
  J1 = female pin header, 2 pins [form="♀ (female)"]
  J2 = female pin header, 2 pins [form="♀ (female)"]
  J3 = female pin header, 2 pins [form="♀ (female)"]
  J4 = female pin header, 2 pins [form="♀ (female)"]
  D1 = Rectifier Diode [part_number=1N4001 package="300 mil [THT]"]

nets:
  N1: Součástka1.GND, R1.Pin_1, R2.Pin_1, R3.Pin_1, R4.Pin_0, D1.anode
  N2: Součástka1.D5, R1.Pin_0, J3.pin2
  N3: Součástka1.D6, R2.Pin_0, J2.pin2
  N4: Součástka1.D7, R3.Pin_0, J1.pin2
  N5: Součástka1.D8, Q1.gate, R4.Pin_1
  N6: Součástka1.VIN, VCC1.+, J4.pin2
  N7: Součástka1.5V, J1.pin1, J2.pin1, J3.pin1
  N8: VCC1.-, Q1.source, D1.cathode
  N9: Q1.drain, J4.pin1
